// Logisim project RIIPLE CARRY ADDER.circ as structural Verilog: 1 circuit, main circuit main
module main (
  input  [3:0] A,
  input  C_IN,
  input  [3:0] B,
  output [3:0] SUM,
  output C_OUT
);

  wire adder_1_cout, adder_2_cout, adder_3_cout;

  Adder #(.width(1)) adder_1 (.a(A[0]), .b(B[0]), .out(SUM[0]), .cin(C_IN), .cout(adder_1_cout));
  Adder #(.width(1)) adder_2 (.a(A[1]), .b(B[1]), .out(SUM[1]), .cin(adder_1_cout), .cout(adder_2_cout));
  Adder #(.width(1)) adder_3 (.a(A[2]), .b(B[2]), .out(SUM[2]), .cin(adder_2_cout), .cout(adder_3_cout));
  Adder #(.width(1)) adder_4 (.a(A[3]), .b(B[3]), .out(SUM[3]), .cin(adder_3_cout), .cout(C_OUT));
endmodule
