// Logisim project SANTWAN 3 AUG 4 BIT ARTHIMETRIC UNIT.circ as structural Verilog: 1 circuit, main circuit main
module main (
  input  in_1,
  input  [1:0] in_2,
  input  in_3,
  input  [3:0] in_4,
  input  in_5,
  input  in_6,
  input  in_7,
  input  in_8,
  input  in_9,
  output out_10,
  output out_11,
  output out_12,
  output out_13,
  output out_14
);

  wire adder_1_cout, adder_2_cout, adder_3_cout, multiplexer_1_out, multiplexer_2_out, multiplexer_3_out,
       multiplexer_4_out, not_1_out, not_2_out, not_3_out, not_4_out;

  not not_1 (not_1_out, in_5);
  not not_2 (not_2_out, in_6);
  not not_3 (not_3_out, in_7);
  not not_4 (not_4_out, in_8);
  Multiplexer #(.select(2), .enable("false")) multiplexer_1 (
    .in0(in_5), .in1(not_1_out), .in2(in_3), .in3(in_9), .out(multiplexer_1_out), .sel(in_2));
  Multiplexer #(.select(2), .enable("false")) multiplexer_2 (
    .in0(in_6), .in1(not_2_out), .in2(in_3), .in3(in_9), .out(multiplexer_2_out), .sel(in_2));
  Multiplexer #(.select(2), .enable("false")) multiplexer_3 (
    .in0(in_7), .in1(not_3_out), .in2(in_3), .in3(in_9), .out(multiplexer_3_out), .sel(in_2));
  Multiplexer #(.select(2), .enable("false")) multiplexer_4 (
    .in0(in_8), .in1(not_4_out), .in2(in_3), .in3(in_9), .out(multiplexer_4_out), .sel(in_2));
  Adder #(.width(1)) adder_1 (.a(in_4[0]), .b(multiplexer_1_out), .out(out_10), .cin(in_1), .cout(adder_1_cout));
  Adder #(.width(1)) adder_2 (
    .a(in_4[1]), .b(multiplexer_2_out), .out(out_11), .cin(adder_1_cout), .cout(adder_2_cout));
  Adder #(.width(1)) adder_3 (
    .a(in_4[2]), .b(multiplexer_3_out), .out(out_12), .cin(adder_2_cout), .cout(adder_3_cout));
  Adder #(.width(1)) adder_4 (.a(in_4[3]), .b(multiplexer_4_out), .out(out_13), .cin(adder_3_cout), .cout(out_14));
endmodule
